// Logisim project single_cycle.circ as structural Verilog: 17 circuits, main circuit main
module main (
);

  wire eq, gt, is_beq, is_bge, is_blt, is_bne, is_jump, lt, mod_decode_1_cmpu, mod_decode_1_is_shift,
       mod_decode_1_load_u, mod_decode_1_mr, mod_decode_1_mw, mod_decode_1_op1_sel, mod_decode_1_op2_sel,
       mod_decode_1_reg_we;
  wire [1:0] wb_sel;
  wire [2:0] mod_decode_1_inst_type;
  wire [3:0] mod_decode_1_alu_sel;
  wire [4:0] mod_decode_1_rs1_sel, mod_decode_1_rs2_sel, mod_decode_1_wr_sel;
  wire [31:0] dnpc, mod_alu_1_alu_out, mod_if_1_inst, mod_imm_gen_1_imm, mod_mem_1_mem_out, mod_pc_1_pc,
       mod_reg_1_rs1, mod_reg_1_rs2, snpc, wb_data;

  mod_pc mod_pc_1 (.dnpc(dnpc), .pc(mod_pc_1_pc), .snpc(snpc));
  mod_if mod_if_1 (.pc(mod_pc_1_pc), .inst(mod_if_1_inst));
  mod_decode mod_decode_1 (
    .inst(mod_if_1_inst), .rs1_sel(mod_decode_1_rs1_sel), .rs2_sel(mod_decode_1_rs2_sel),
    .wr_sel(mod_decode_1_wr_sel), .reg_we(mod_decode_1_reg_we), .op1_sel(mod_decode_1_op1_sel),
    .op2_sel(mod_decode_1_op2_sel), .alu_sel(mod_decode_1_alu_sel), .mr(mod_decode_1_mr),
    .mw(mod_decode_1_mw), .is_beq(is_beq), .is_bne(is_bne), .is_blt(is_blt), .is_bge(is_bge),
    .is_jump(is_jump), .wb_sel(wb_sel), .cmpU(mod_decode_1_cmpu), .is_shift(mod_decode_1_is_shift),
    .inst_type(mod_decode_1_inst_type), .load_U(mod_decode_1_load_u));
  mod_reg mod_reg_1 (
    .rs1_sel(mod_decode_1_rs1_sel), .rs2_sel(mod_decode_1_rs2_sel), .wr_sel(mod_decode_1_wr_sel),
    .reg_we(mod_decode_1_reg_we), .data_in(wb_data), .rs1(mod_reg_1_rs1), .rs2(mod_reg_1_rs2));
  mod_imm_gen mod_imm_gen_1 (
    .is_shift(mod_decode_1_is_shift), .inst_type(mod_decode_1_inst_type), .inst(mod_if_1_inst),
    .imm(mod_imm_gen_1_imm));
  mod_alu mod_alu_1 (
    .pc(mod_pc_1_pc), .rs1(mod_reg_1_rs1), .rs2(mod_reg_1_rs2), .op1_sel(mod_decode_1_op1_sel),
    .op2_sel(mod_decode_1_op2_sel), .alu_sel(mod_decode_1_alu_sel), .is_shift(mod_decode_1_is_shift),
    .imm(mod_imm_gen_1_imm), .alu_out(mod_alu_1_alu_out));
  mod_cmp mod_cmp_1 (.op1(mod_reg_1_rs1), .op2(mod_reg_1_rs2), .cmpU(mod_decode_1_cmpu), .lt(lt), .eq(eq), .gt(gt));
  mod_mem mod_mem_1 (
    .addr(mod_alu_1_alu_out), .mr(mod_decode_1_mr), .mw(mod_decode_1_mw), .load_U(mod_decode_1_load_u),
    .mem_out(mod_mem_1_mem_out));
  mod_wb_pc mod_wb_pc_1 (
    .snpc(snpc), .alu(mod_alu_1_alu_out), .is_beq(is_beq), .is_bne(is_bne), .is_blt(is_blt), .is_bge(is_bge),
    .is_jump(is_jump), .lt(lt), .eq(eq), .gt(gt), .dnpc(dnpc));
  mod_wb_reg mod_wb_reg_1 (
    .alu(mod_alu_1_alu_out), .mem(mod_mem_1_mem_out), .snpc(snpc), .wb_data_sel(wb_sel), .wb_data(wb_data));
endmodule

module mod_pc (
  input  [31:0] dnpc,
  output [31:0] pc,
  output [31:0] snpc
);

  Register #(.width(32)) register_1 (.D(dnpc), .Q(pc));  // open: en, clk, clr
  Adder #(.width(32)) adder_1 (.a(32'h4), .b(pc), .out(snpc));  // open: cin, cout
endmodule

module mod_reg (
  input  [4:0] rs1_sel,
  input  [4:0] rs2_sel,
  input  [4:0] wr_sel,
  input  reg_we,
  input  [31:0] data_in,
  output [31:0] rs1,
  output [31:0] rs2
);
endmodule

module mod_if (
  input  [31:0] pc,
  output [31:0] inst
);
endmodule

module mod_decode (
  input  [31:0] inst,
  output [4:0] rs1_sel,
  output [4:0] rs2_sel,
  output [4:0] wr_sel,
  output reg_we,
  output op1_sel,
  output op2_sel,
  output [3:0] alu_sel,
  output mr,
  output mw,
  output is_beq,
  output is_bne,
  output is_blt,
  output is_bge,
  output is_jump,
  output [1:0] wb_sel,
  output cmpU,
  output is_shift,
  output [2:0] inst_type,
  output load_U
);
endmodule

module mod_mem (
  input  [31:0] addr,
  input  mr,
  input  mw,
  input  load_U,
  output [31:0] mem_out
);
endmodule

module mod_alu (
  input  [31:0] pc,
  input  [31:0] rs1,
  input  [31:0] rs2,
  input  op1_sel,
  input  op2_sel,
  input  [3:0] alu_sel,
  input  is_shift,
  input  [31:0] imm,
  output [31:0] alu_out
);
endmodule

module mod_cmp (
  input  [31:0] op1,
  input  [31:0] op2,
  input  cmpU,
  output lt,
  output eq,
  output gt
);
endmodule

module mod_imm_gen (
  input  is_shift,
  input  [2:0] inst_type,
  input  [31:0] inst,
  output [31:0] imm
);

  mod_immI mod_immi_1 (.inst(inst));  // open: immI
  mod_immI_shamt mod_immi_shamt_1 (.inst(inst));  // open: immI_shamt
  mod_ImmU mod_immu_1 (.inst(inst));  // open: immU
  mod_immS mod_imms_1 (.inst(inst));  // open: immS
  mod_immB mod_immb_1 (.inst(inst));  // open: immB
  mod_immJ mod_immj_1 (.inst(inst));  // open: immJ
endmodule

module mod_immI (
  input  [31:0] inst,
  output [31:0] immI
);
endmodule

module mod_ImmU (
  input  [31:0] inst,
  output [31:0] immU
);
endmodule

module mod_immS (
  input  [31:0] inst,
  output [31:0] immS
);
endmodule

module mod_immB (
  input  [31:0] inst,
  output [31:0] immB
);
endmodule

module mod_immJ (
  input  [31:0] inst,
  output [31:0] immJ
);
endmodule

module mod_immI_shamt (
  input  [31:0] inst,
  output [31:0] immI_shamt
);
endmodule

module mod_wb_reg (
  input  [31:0] alu,
  input  [31:0] mem,
  input  [31:0] snpc,
  input  [1:0] wb_data_sel,
  output [31:0] wb_data
);
endmodule

module mod_wb_pc (
  input  [31:0] snpc,
  input  [31:0] alu,
  input  is_beq,
  input  is_bne,
  input  is_blt,
  input  is_bge,
  input  is_jump,
  input  lt,
  input  eq,
  input  gt,
  output [31:0] dnpc
);
endmodule
